# Fritzing sketch DataLogger (saved by Fritzing 0.9.3b)
breadboards: 2

parts:
  Part1 = Arduino Uno (Rev3) - ICSP
  LCD1 = LCD screen
  R1 = Rotary Potentiometer (Large) [maximum_resistance=100kΩ package=THT]
  S2 = Momentary Switch [package=ksa_sealed_tac_switch]
  R2 = Resistor [tolerance=±5% resistance=220 package="0402 [SMD]"]
  R3 = Resistor [tolerance=±5% resistance=220 package="0402 [SMD]"]
  R4 = Temperature Sensor (Thermistor) [thermistor_type=NTC package=THT]
  LED1 = LED - 5mm [color="Red (633nm)" package="5 mm [THT]"]
  Part2 = MicroSD Card Module

nets:
  N1: Part1.A0, R3.Pin_0, R4.pin_1
  N2: Part1.A1, R1.wiper
  N3: Part1.A4/SDA, LCD1.DB7
  N4: Part1.A5/SCL, LCD1.DB6
  N5: Part1.ICSP_MISO, Part1.D12/MISO, Part2.MISO
  N6: Part1.D10_PWM/SS, LED1.cathode
  N7: Part1.D11_PWM/MOSI, Part2.MOSI
  N8: Part1.D13/SCK, Part2.SCK
  GND: Part1.GND, LCD1.LED-, R1.leg2, R2.Pin_1, R3.Pin_1, LED1.anode, Part2.GND
  N9: Part1.D2, S2.1
  N10: Part1.D4, Part2.CS
  5V: Part1.5V, LCD1.LED+, R1.leg1, S2.4, R4.pin_0, Part2.VCC
  N11: S2.2, R2.Pin_0

notes:
  LCM1602 IIC daughter board allowing four wires to connect LCD - the 16 pin connector I use here isn't needed
  SCL = A5
  SDA = A4
