# Fritzing sketch Glove (saved by Fritzing 0.9.3b)
breadboards: 1

parts:
  Part1 = Arduino Uno (Rev3) - ICSP
  R1 = Photocell (LDR) [package=THT]
  R2 = Photocell (LDR) [package=THT]
  R3 = Photocell (LDR) [package=THT]
  R4 = Photocell (LDR) [package=THT]
  R5 = Photocell (LDR) [package=THT]

nets:
  N1: Part1.A0, R1.pin_1
  N2: Part1.A2, R3.pin_1
  N3: Part1.A3, R4.pin_1
  N4: Part1.5V, R1.pin_0, R2.pin_0, R3.pin_0, R4.pin_0, R5.pin_0
