# Fritzing sketch KnexBot_soFar (saved by Fritzing 0.9.3b)
breadboards: 1

parts:
  LED1 = LED - 5mm [color="Red (633nm)" package="5 mm [THT]"]
  LED2 = LED - 5mm [color="Red (633nm)" package="5 mm [THT]"]
  LED3 = LED - 5mm [color="Red (633nm)" package="5 mm [THT]"]
  LED4 = LED - 5mm [color="Red (633nm)" package="5 mm [THT]"]
  LED5 = LED - 5mm [color="Red (633nm)" package="5 mm [THT]"]
  LED6 = LED - 5mm [color="Red (633nm)" package="5 mm [THT]"]
  Part1 = Bluetooth HC-05 Macho  # not connected
  Part2 = Arduino Uno (Rev3)
  hc-sr1 = hc-sr04
  LCD1 = LCD screen
  LED7 = LED - 5mm [color="Red (633nm)" package="5 mm [THT]"]
  LED8 = LED - 5mm [color="Red (633nm)" package="5 mm [THT]"]
  LED9 = LED - 5mm [color="Red (633nm)" package="5 mm [THT]"]
  LED10 = LED - 5mm [color="Red (633nm)" package="5 mm [THT]"]
  Part3 = Bluetooth HC-05 Macho
  Part4 = Arduino Leonardo (Rev3b)
  SP1 = SPEAKER [package=pcb_mount_speaker]

nets:
  N1: LED1.cathode, LED2.cathode, LED3.cathode, LED4.cathode, LED5.cathode, LED6.anode
  N2: LED1.anode, LED2.anode, LED4.anode, LED5.anode, LED6.cathode
  N3: Part2.A4/SDA, LCD1.DB7
  N4: Part2.A5/SCL, LCD1.DB4
  N5: Part2.D12/MISO, hc-sr1.Echo
  N6: Part2.D13/SCK, hc-sr1.Trig
  GND: Part2.GND, hc-sr1.GND, LED10.cathode
  N7: Part2.D0/RX, Part3.TXD
  N8: Part2.D1/TX, Part3.RXD
  N9: Part2.D2, LED9.anode
  N10: Part2.D3_PWM, LED8.anode
  N11: Part2.D4, LED7.anode
  N12: Part2.D5_PWM, LED10.anode
  N13: Part2.D7, Part4.D3_PWM/SCL
  VCC: Part2.5V, hc-sr1.VCC, LCD1.VDD, LCD1.LED-, Part3.VCC
  GND_2: Part3.GND, Part4.GND, SP1.+
  N14: Part4.D0/RX, Part4.D6_PWM/A7, SP1.-

notes:
  Chest LED
  Microbit - not Arduino
  Yellow = SDA from daughter board (not shown)
  Green = SCL from daughter board (not shown)
