# Fritzing sketch Morse Code with MicroBit and speaker (saved by Fritzing 0.9.3b)
breadboards: 1

parts:
  Part1 = Arduino Uno (Rev3) - ICSP
  Dot = Momentary Switch [package=tactile-pth]
  Dash = Momentary Switch [package=tactile-pth]
  LED1 = Super Flux LED blue [color=Blue]
  LED2 = Super Flux LED blue [color=Blue]
  Actually_a_Micro_Bit = Arduino Uno (Rev3) - ICSP
  SP1 = SPEAKER [package=pcb_mount_speaker]
  LED3 = Super Flux LED blue [color=Blue]

nets:
  N1: Part1.5V, Dot.2, Dash.2
  N2: Part1.D11_PWM/MOSI, Dash.1, LED1.cathode
  N3: Part1.D12/MISO, Dot.1, LED2.cathode
  GND: Part1.GND, LED1.anode, LED2.anode, Actually_a_Micro_Bit.GND, SP1.+, LED3.anode
  N4: Dot.3, Actually_a_Micro_Bit.D3_PWM
  N5: Actually_a_Micro_Bit.ICSP_MISO, Actually_a_Micro_Bit.D12/MISO, LED3.cathode
  N6: Actually_a_Micro_Bit.D0/RX, SP1.-

notes:
  A bit tenuous, but will help me remember
  Touch wire
