# Fritzing sketch Morse Code (saved by Fritzing 0.9.3b)
breadboards: 1

parts:
  Part1 = Arduino Uno (Rev3) - ICSP
  Dot = Momentary Switch [package=tactile-pth]
  Dash = Momentary Switch [package=tactile-pth]
  LED1 = Super Flux LED blue [color=Blue]
  LED2 = Super Flux LED blue [color=Blue]

nets:
  N1: Part1.5V, Dot.2, Dash.2
  N2: Part1.GND, LED1.anode, LED2.anode
  N3: Part1.D11_PWM/MOSI, Dash.1, LED1.cathode
  N4: Part1.D12/MISO, Dot.1, LED2.cathode
