# Fritzing sketch Robot (saved by Fritzing 0.9.3b)
breadboards: 1

parts:
  IC2 = L293D [package=THT]
  Part1 = Arduino Uno (Rev3) - ICSP
  hc-sr1 = hc-sr04
  BAT1 = Battery Holders [package=battery-aa]
  BAT2 = Battery Holders [package=battery-aa]
  BAT3 = Battery Holders [package=battery-aa]
  BAT4 = BC9VPC [package=bc9vpc]
  Left_Motor = DC Motor
  Right_Motor = DC Motor

nets:
  N1: IC2.Enable_1, IC2.+V, Part1.5V
  N2: IC2.In_1, IC2.In_4, Part1.D2, Part1.D5_PWM
  N3: IC2.Out_1_(_Controlled_by_Enable_1_), IC2.Out_4_(_Controlled_by_Enable_2_), Left_Motor.pin_1, Right_Motor.pin_2
  N4: IC2.0V, Part1.GND, BAT4.V-
  N5: IC2.Out_2_(_Controlled_by_Enable_1_), IC2.Out_3_(_Controlled_by_Enable_2_), Left_Motor.pin_2, Right_Motor.pin_1
  N6: IC2.In_2, IC2.In_3, Part1.D3_PWM, Part1.D4
  N7: IC2.+Vmotor, IC2.Enable_2, BAT4.V+
  N8: Part1.D12/MISO, hc-sr1.Trig
  N9: Part1.D13/SCK, hc-sr1.Echo
  N10: hc-sr1.VCC, BAT1.+
  N11: hc-sr1.GND, BAT3.-
  N12: BAT1.-, BAT2.+
  N13: BAT2.-, BAT3.+

// code stored in the sketch: DuelMotorTestUno.ino

#define trigPin 13
#define echoPin 12
#define leftMotorPinCW 2//in1
#define leftMotorPinCCW 3//in2
#define rightMotorPinCW 4//in3
#define rightMotorPinCCW 5//in4

int randNumber;

void setup() {
  Serial.begin (9600);
  pinMode(trigPin, OUTPUT);
  pinMode(echoPin, INPUT);
  pinMode(leftMotorPinCW, OUTPUT);
  pinMode(rightMotorPinCW, OUTPUT);
  pinMode(leftMotorPinCCW, OUTPUT);
  pinMode(rightMotorPinCCW, OUTPUT);
  randomSeed(analogRead(0));
}


void left(){

  //left
  digitalWrite(leftMotorPinCW,HIGH);
  digitalWrite(rightMotorPinCCW,LOW);
  digitalWrite(leftMotorPinCCW,LOW);
  digitalWrite(rightMotorPinCW,HIGH);
}

void right(){
  //right
  digitalWrite(leftMotorPinCW,LOW);
  digitalWrite(rightMotorPinCCW,HIGH);
  digitalWrite(leftMotorPinCCW,HIGH);
  digitalWrite(rightMotorPinCW,LOW);
}

void backwards(){
  //backwards 
  //digitalWrite(leftMotorPinCW,LOW);
  //digitalWrite(rightMotorPinCCW,HIGH);
  //digitalWrite(leftMotorPinCCW,HIGH);
  //digitalWrite(rightMotorPinCW,LOW);
}

void loop() {
  randNumber = random(2);
  long duration, distance;
  digitalWrite(trigPin, LOW);
  delayMicroseconds(2);
  digitalWrite(trigPin, HIGH);
  delayMicroseconds(10); 
  digitalWrite(trigPin, LOW);
  duration = pulseIn(echoPin, HIGH);
  distance = (duration/2) / 29.1;

  Serial.println(distance);
  //forwards
  digitalWrite(leftMotorPinCW,HIGH);
  digitalWrite(rightMotorPinCW,HIGH);
  digitalWrite(leftMotorPinCCW,LOW);
  digitalWrite(rightMotorPinCCW,LOW);
  Serial.println("forwards");

  
  //something close by
  if (distance < 30) {
    //need to turn - random
    if (randNumber == 0){
      Serial.println("turning left");
      left();
    }
    else{
      Serial.println("turning right");
      right();
      
    } 
  }
}
